// Logisim project control_logic.circ as structural Verilog: 1 circuit, main circuit control_logic
module control_logic (
  input  [31:0] inst,
  input  BrEq,
  input  BrLt,
  output PCSel,
  output RegWEn,
  output [2:0] ImmSel,
  output BrUn,
  output ASel,
  output BSel,
  output [3:0] ALUSel,
  output MemRW,
  output [1:0] WBSel,
  output CSRSel,
  output CSRWen
);

  wire brSel, or_1_out, RomPCSel;

  ROM #(.addrWidth(12), .dataWidth(18)) rom_1 (
    .addr({inst[30], inst[25], inst[14:12], inst[6:0]}),
    .data({brSel, CSRWen, CSRSel, WBSel, MemRW, ALUSel, BSel, ASel, BrUn, ImmSel, RegWEn, RomPCSel}));
  or or_1 (or_1_out, BrEq, BrLt);
  Multiplexer #(.enable("false")) multiplexer_1 (.in0(RomPCSel), .in1(or_1_out), .out(PCSel), .sel(brSel));

  // Other names for the same wires on the sheet: opcode[6:0] = inst[6:0]; func3[2:0] = inst[14:12];
  //   func7[6:0] = inst[31:25]

  // Notes on the sheet:
  //   INPUTS to your circuit
  //   DON'T CHANGE THE LOCATIONS OF THE INPUTS AND OUTPUTS!
  //   OUTPUT from your circuit
endmodule
