// Logisim project cpu.circ as structural Verilog: 1 circuit, main circuit cpu
module cpu (
  input  clk,
  input  [31:0] INSTRUCTION,
  input  [31:0] READ_DATA,
  output [31:0] WRITE_ADDRESS,
  output [31:0] PROGRAM_COUNTER,
  output [31:0] ra,
  output [31:0] sp,
  output [31:0] t0,
  output [31:0] t1,
  output [31:0] t2,
  output [31:0] s0,
  output [31:0] s1,
  output [31:0] a0,
  output [31:0] tohost,
  output [3:0] WRITE_ENABLE,
  output [31:0] WRITE_DATA
);

  wire ASel, brEq, brLt, brUn, BSel, CSRSel, CSRWen, MemRw, PCSel, RegEn;
  wire [1:0] WBSel;
  wire [2:0] ImmSel;
  wire [3:0] ALUSel;
  wire [4:0] rd, RD_EX_q, rs1, rs2;
  wire [11:0] imm;
  wire [14:0] INST_ID0_q;
  wire [31:0] adder_1_out, ALU_OUTPUT, imm32, multiplexer_1_out, rs1_data, RS1_EX_q, rs2_data, RS2_EX_q;

  Adder #(.width(32)) adder_1 (.a(PROGRAM_COUNTER), .b(32'h4), .out(adder_1_out));  // open: cin, cout
  Register #(.width(32)) PC (.D(adder_1_out), .clk(clk), .Q(PROGRAM_COUNTER));  // open: en, clr
  Register #(.width(32)) INST_ID0 (
    .D(INSTRUCTION), .clk(clk), .Q({imm, rs1, INST_ID0_q[14:12], rd, INST_ID0_q[6:0]}));  // open: en, clr
  control_logic control_logic_1 (
    .CSRWen(CSRWen), .PCSel(PCSel), .RegWEn(RegEn), .ImmSel(ImmSel), .BrUn(brUn), .ASel(ASel), .BSel(BSel),
    .ALUSel(ALUSel), .MemRW(MemRw), .WBSel(WBSel), .CSRSel(CSRSel), .inst(INSTRUCTION), .BrEq(brEq),
    .BrLt(brLt));
  Register #(.width(5)) RD_EX (.D(rd), .clk(clk), .Q(RD_EX_q));  // open: en, clr
  imm_gen imm_gen_1 (.inst({imm, rs1, INST_ID0_q[14:12], rd, INST_ID0_q[6:0]}), .ImmSel(ImmSel), .imm(imm32));
  branch_comp branch_comp_1 (.rs1(rs1_data), .rs2(rs2_data), .BrEq(brEq), .BrLt(brLt));  // open: BrUn
  regfile regfile_1 (
    .rs1(rs1), .rs2(rs2), .rd(RD_EX_q), .Write_Data(ALU_OUTPUT), .RegWEn(RegEn), .clk(clk), .ra(ra), .sp(sp),
    .t0(t0), .t1(t1), .t2(t2), .s0(s0), .s1(s1), .a0(a0), .Read_Data_1(rs1_data), .Read_Data_2(rs2_data));
  csr csr_1 (.tohost(tohost));  // open: CSR_address, CSR_din, CSR_WE, clk
  Register #(.width(32)) RS2_EX (.D(rs2_data), .clk(clk), .Q(RS2_EX_q));  // open: en, clr
  Register #(.width(32)) RS1_EX (.D(rs1_data), .clk(clk), .Q(RS1_EX_q));  // open: en, clr
  Multiplexer #(.enable("false"), .width(32)) multiplexer_1 (
    .in0(RS2_EX_q), .in1(imm32), .out(multiplexer_1_out), .sel(BSel));
  alu alu_1 (.Result(ALU_OUTPUT), .A(RS1_EX_q), .B(multiplexer_1_out), .ALUSel(ALUSel));

  // Notes on the sheet:
  //   Output to IMEM
  //   IMEM (do **NOT** move this)
  //   Inputs from IMEM
  //   Inputs/Outputs for testing. Do **NOT** move these.
  //   Outputs To DMEM
  //   DMEM (do **NOT** move this)
  //   Inputs From DMEM
endmodule
